// Digital circuit 16-BIT-LOOKAHEADADDER.dig as structural Verilog
module _16_BIT_LOOKAHEADADDER (
  input  [15:0] A,
  input  [15:0] B,
  input  Ci,
  output [15:0] S,
  output Cout
);

  wire _4_bit_lookaheadadder_1_p1, _4_bit_lookaheadadder_1_p8, _4_bit_lookaheadadder_1_p9,
       _4_bit_lookaheadadder_2_p1, _4_bit_lookaheadadder_2_p8, _4_bit_lookaheadadder_2_p9,
       _4_bit_lookaheadadder_3_p8, _4_bit_lookaheadadder_3_p9, _4_bit_lookaheadadder_4_p8,
       _4_bit_lookaheadadder_4_p9, clu_1_c0;

  // _4_bit_LOOKAHEADADDER _4_bit_lookaheadadder_1: pin names not known; wires that end beside it: _4_bit_lookaheadadder_1_p1, A[15:12], B[15:12], S[12], S[13], S[14], S[15], _4_bit_lookaheadadder_1_p8, _4_bit_lookaheadadder_1_p9
  // _4_bit_LOOKAHEADADDER _4_bit_lookaheadadder_2: pin names not known; wires that end beside it: _4_bit_lookaheadadder_2_p1, A[11:8], B[11:8], S[8], S[9], S[10], S[11], _4_bit_lookaheadadder_2_p8, _4_bit_lookaheadadder_2_p9
  CLU clu_1 (
    .Ci(Ci), .G0(_4_bit_lookaheadadder_4_p9), .P0(_4_bit_lookaheadadder_4_p8),
    .G1(_4_bit_lookaheadadder_3_p9), .P1(_4_bit_lookaheadadder_3_p8), .G2(_4_bit_lookaheadadder_2_p9),
    .P2(_4_bit_lookaheadadder_2_p8), .G3(_4_bit_lookaheadadder_1_p9), .P3(_4_bit_lookaheadadder_1_p8),
    .C0(clu_1_c0), .C1(_4_bit_lookaheadadder_2_p1), .C2(_4_bit_lookaheadadder_1_p1), .C3(Cout));
  // _4_bit_LOOKAHEADADDER _4_bit_lookaheadadder_3: pin names not known; wires that end beside it: clu_1_c0, A[7:4], B[7:4], S[4], S[5], S[6], S[7], _4_bit_lookaheadadder_3_p8, _4_bit_lookaheadadder_3_p9
  // _4_bit_LOOKAHEADADDER _4_bit_lookaheadadder_4: pin names not known; wires that end beside it: Ci, A[3:0], B[3:0], S[0], S[1], S[2], S[3], _4_bit_lookaheadadder_4_p8, _4_bit_lookaheadadder_4_p9
endmodule
