// Digital circuit 4-bit-LOOKAHEADADDER.dig as structural Verilog
module _4_bit_LOOKAHEADADDER (
  input  Ci,
  input  [3:0] A,
  input  [3:0] B,
  output S0,
  output S1,
  output S2,
  output S3,
  output C3,
  output Pm,
  output Gm
);

  wire clu_1_c0, clu_1_c1, clu_1_c2, pg_1_g, pg_1_p, pg_2_g, pg_2_p, pg_3_g, pg_3_p, pg_4_g, pg_4_p,
       xor_1_out, xor_2_out, xor_3_out, xor_4_out;

  PG pg_1 (.A(A[0]), .B(B[0]), .G(pg_1_g), .P(pg_1_p));
  PG pg_2 (.A(A[1]), .B(B[1]), .G(pg_2_g), .P(pg_2_p));
  PG pg_3 (.A(A[2]), .B(B[2]), .G(pg_3_g), .P(pg_3_p));
  PG pg_4 (.A(A[3]), .B(B[3]), .G(pg_4_g), .P(pg_4_p));
  xor xor_1 (xor_1_out, A[0], B[0]);
  xor xor_2 (xor_2_out, A[1], B[1]);
  xor xor_3 (xor_3_out, A[2], B[2]);
  xor xor_4 (xor_4_out, A[3], B[3]);
  CLU clu_1 (
    .Ci(Ci), .G0(pg_1_g), .P0(pg_1_p), .G1(pg_2_g), .P1(pg_2_p), .G2(pg_3_g), .P2(pg_3_p), .G3(pg_4_g),
    .P3(pg_4_p), .C0(clu_1_c0), .C1(clu_1_c1), .C2(clu_1_c2), .C3(C3));
  xor xor_5 (S0, Ci, xor_1_out);
  xor xor_6 (S1, xor_2_out, clu_1_c0);
  xor xor_7 (S2, xor_3_out, clu_1_c1);
  xor xor_8 (S3, xor_4_out, clu_1_c2);
  PGM pgm_1 (
    .G0(pg_1_g), .P0(pg_1_p), .G1(pg_2_g), .P1(pg_2_p), .G2(pg_3_g), .P2(pg_3_p), .G3(pg_4_g), .P3(pg_4_p),
    .Pm(Pm), .Gm(Gm));
  // Pins of 1 and 4 bits meet at A
  // Pins of 1 and 4 bits meet at B
endmodule
