// Digital circuit CLU.dig as structural Verilog
module CLU (
  input  Ci,
  input  G0,
  input  P0,
  input  G1,
  input  P1,
  input  G2,
  input  P2,
  input  G3,
  input  P3,
  output C0,
  output C1,
  output C2,
  output C3
);

  wire and_1_out, and_2_out, and_3_out, and_4_out, and_5_out, and_6_out, and_7_out, and_8_out, and_9_out,
       and_10_out;

  and and_1 (and_1_out, P0, Ci);
  and and_2 (and_2_out, P0, P1, Ci);
  and and_3 (and_3_out, G0, P1);
  and and_4 (and_4_out, G1, P2);
  and and_5 (and_5_out, G0, P1, P2);
  and and_6 (and_6_out, P0, P1, P2, Ci);
  and and_7 (and_7_out, G2, P3);
  and and_8 (and_8_out, G1, P2, P3);
  and and_9 (and_9_out, G0, P1, P2, P3);
  and and_10 (and_10_out, P0, P1, P2, P3, Ci);
  or or_1 (C0, and_1_out, G0);
  or or_2 (C1, and_2_out, and_3_out, G1);
  or or_3 (C2, and_4_out, and_5_out, and_6_out, G2);
  or or_4 (C3, and_7_out, and_8_out, and_9_out, and_10_out, G3);
endmodule
