// Digital circuit PGM.dig as structural Verilog
module PGM (
  input  G0,
  input  P0,
  input  G1,
  input  P1,
  input  G2,
  input  P2,
  input  G3,
  input  P3,
  output Pm,
  output Gm
);

  wire and_1_out, and_2_out, and_3_out;

  and and_1 (and_1_out, G2, P3);
  and and_2 (and_2_out, G1, P2, P3);
  and and_3 (and_3_out, G0, P1, P2, P3);
  or or_1 (Gm, G3, and_1_out, and_2_out, and_3_out);
  and and_4 (Pm, P3, P2, P1, P0);
endmodule
