// Digital circuit extended-lookahead-alu.dig as structural Verilog
module extended_lookahead_alu (
  input  [15:0] A,
  input  [15:0] B,
  input  [1:0] ALUOP,
  output [15:0] RESULT,
  output [3:0] FLAG
);

  wire _16_bit_lookaheadadder_1_cout, and_2_out, multiplexer_3_out, xnor_1_out, xor_1_out;
  wire [15:0] _16_bit_lookaheadadder_1_s, and_1_out, demultiplexer_1_out_0, demultiplexer_1_out_1,
       multiplexer_1_out, multiplexer_2_out, not_1_out, or_1_out;

  assign not_1_out = ~B;  // Not not_1, 16 bits wide
  assign and_1_out = A & B;  // And and_1, 16 bits wide
  assign or_1_out = A | B;  // Or or_1, 16 bits wide
  Multiplexer #(.Selector_Bits(2), .Bits(16)) multiplexer_1 (
    .sel(ALUOP), .in_0(B), .in_1(not_1_out), .in_2({16{1'b0}}), .in_3({16{1'b0}}), .out(multiplexer_1_out));
  Multiplexer #(.Bits(16)) multiplexer_2 (.sel(ALUOP[0]), .in_0(B), .in_1(not_1_out), .out(multiplexer_2_out));
  Multiplexer multiplexer_3 (.sel(ALUOP[0]), .in_0(1'b0), .in_1(1'b1), .out(multiplexer_3_out));
  _16_BIT_LOOKAHEADADDER _16_bit_lookaheadadder_1 (
    .A(A), .B(multiplexer_2_out), .Ci(multiplexer_3_out), .S(_16_bit_lookaheadadder_1_s),
    .Cout(_16_bit_lookaheadadder_1_cout));
  Demultiplexer #(.Bits(16)) demultiplexer_1 (
    .sel(ALUOP[0]), .in(_16_bit_lookaheadadder_1_s), .out_0(demultiplexer_1_out_0),
    .out_1(demultiplexer_1_out_1));
  Multiplexer #(.Selector_Bits(2), .Bits(16)) multiplexer_4 (
    .sel(ALUOP), .in_0(demultiplexer_1_out_0), .in_1(demultiplexer_1_out_1), .in_2(and_1_out),
    .in_3(or_1_out), .out({FLAG[1], RESULT[14:0]}));
  nor nor_1 (FLAG[0], RESULT[0], RESULT[1], RESULT[2], RESULT[3], RESULT[4], RESULT[5], RESULT[6], RESULT[7], RESULT[8], RESULT[9], RESULT[10], RESULT[11], RESULT[12], RESULT[13], RESULT[14], FLAG[1]);
  Multiplexer multiplexer_5 (.sel(ALUOP[1]), .in_0(_16_bit_lookaheadadder_1_cout), .in_1(1'b0), .out(FLAG[2]));
  xor xor_1 (xor_1_out, A[15], FLAG[1]);
  xnor xnor_1 (xnor_1_out, multiplexer_1_out[15], A[15]);
  and and_2 (and_2_out, xnor_1_out, xor_1_out);
  Multiplexer multiplexer_6 (.sel(ALUOP[1]), .in_0(and_2_out), .in_1(1'b0), .out(FLAG[3]));

  assign RESULT[15] = FLAG[1];

  // Notes on the sheet:
  //   A: First input to ALU
  //   B: Second input to ALU
  //   ALUOP: Operation selection input
  //   RESULT: The result of this ALU operation
  //   FLAG: The flags associated with the result of this ALU operation
  //   0. Z (zero)
  //   1. N (negative)
  //   2. C (carry)
  //   3. V (overflow)
endmodule

/* Test case RESULT:
ALUOP A B RESULT

# Test small results
loop(a, 1 << 4)
loop(b, 1 << 4)
    (00) (a) (b) ((a + b) & 0xFFFF)
    (01) (a) (b) ((a - b) & 0xFFFF)
    (10) (a) (b) (a & b)
    (11) (a) (b) (a | b)
end loop
end loop


# Test large results
loop(i, 1000)
    let a = random(1 << 16);
    let b = random(1 << 16);

    (00) (a) (b) ((a + b) & 0xFFFF)
    (01) (a) (b) ((a - b) & 0xFFFF)
    (10) (a) (b) (a & b)
    (11) (a) (b) (a | b)
end loop
*/

/* Test case Z:
ALUOP A B Z

declare Z = FLAG & 0b1;

# Test all zero cases
00 0 0 1
01 0 0 1
10 0 0 1
11 0 0 1

# Test 1 + (-1) = 0
00 1 0xFFFF 1

# Test with a single bit set in A
loop(s, 16)
    let a = 1 << s;

    00 (a) 0 (a = 0)
    01 (a) 0 (a = 0)
    10 (a) 0 1
    11 (a) 0 (a = 0)
end loop

# Test random inputs
loop(i, 200)
    let a = random(1 << 16);
    let b = random(1 << 16);

    00 (a) (b) (((a + b) & 0xFFFF) = 0)
    01 (a) (b) (((a - b) & 0xFFFF) = 0)
    10 (a) (b) ((a & b) = 0)
    11 (a) (b) ((a | b) = 0)
end loop
*/

/* Test case N:
ALUOP A B N

declare N = (FLAG >> 1) & 0b1;

# Test all zero cases
00 0 0 0
01 0 0 0
10 0 0 0
11 0 0 0

00 1 0xFFFF 0

# Test with a single bit set in A
loop(s, 16)
    let a = 1 << s;

    00 (a) 0 ((a >> 15) & 0b1)
    01 (a) 0 ((a >> 15) & 0b1)
    10 (a) 0 0
    11 (a) 0 ((a >> 15) & 0b1)
end loop

# Test random inputs
loop(i, 200)
    let a = random(1 << 16);
    let b = random(1 << 16);

    00 (a) (b) (((a + b) >> 15) & 0b1)
    01 (a) (b) (((a - b) >> 15) & 0b1)
    10 (a) (b) (((a & b) >> 15) & 0b1)
    11 (a) (b) (((a | b) >> 15) & 0b1)
end loop
*/

/* Test case C:
ALUOP A B C

declare C = (FLAG >> 2) & 0b1;

00 0 0 0

# (0 - 0) is implemented as 0 + (0xFFFF + 1), so a carry is expected
01 0 0 1

# Carry should propagate all the way from the first bit if necessary
00 1 0xFFFF 1

# Test with a single bit set in A
loop(s, 16)
    let a = 1 << s;

    00 (a) 0 0
    01 (a) 0 1  # (a - 0) is implemented as (a + 0xFFFF + 1) in the adder, so a carry is always expected
    10 (a) 0 0  # carry is defined as 0 for AND
    11 (a) 0 0  # carry is defined as 0 for OR
end loop

# Adding 15 bit values should never carry
loop(i, 100)
    00 (random(1 << 15)) (random(1 << 15)) 0
end loop

# Test random inputs
loop(i, 200)
    let a = random(1 << 16);
    let b = random(1 << 16);

    00 (a) (b) (((a + b) >> 16) & 0b1)
    01 (a) (b) (~((a - b) >> 16) & 0b1)
end loop

# AND and OR never set carry
loop(i, 100)
    let a = random(1 << 16);
    let b = random(1 << 16);
    10 (a) (b) 0
    11 (a) (b) 0
end loop
*/

/* Test case V:
ALUOP A B V

declare V = (FLAG >> 3) & 0b1;

00 0 0 0
01 0 0 0

# 1 + (-1) = 0  ; different input signs = no overflow here!
00 1 0xFFFF 0

# 3 - 5 = 3 + (-5) = -2  ; subtraction inverts the second operand sign
01 3 5 0

# Some edge cases when subtracting 0x8000
01 0x8000 0x8000 0
01 0xFFFF 0x8000 0
01 0x7FFF 0x8000 1

# Test with a single bit set in A
loop(s, 16)
    let a = 1 << s;

    00 (a) 0 0
    01 (a) 0 0
    10 (a) 0 0  # overflow is defined as 0 for AND
    11 (a) 0 0  # overflow is defined as 0 for OR
end loop

# Test random inputs
loop(i, 200)
    let a = random(1 << 16);
    let b = random(1 << 16);

    00 (a) (b) (((~(a ^ b) & (a ^ (a + b))) >> 15) & 0b1)
    01 (a) (b) (((~(a ^ -b) & (a ^ (a - b))) >> 15) & 0b1)
end loop

# AND and OR never set overflow
loop(i, 100)
    let a = random(1 << 16);
    let b = random(1 << 16);
    10 (a) (b) 0
    11 (a) (b) 0
end loop
*/
