// Digital circuit extended-reg-file.dig as structural Verilog
module extended_reg_file (
  input  [3:0] RS1,
  input  [3:0] RS2,
  input  [3:0] WS,
  input  WE,
  input  [15:0] IN,
  input  clk,
  input  FLEN,
  input  [15:0] FLIN,
  input  [15:0] R7,
  output [15:0] OUT1,
  output [15:0] OUT2,
  output [15:0] FLOUT
);

  wire demultiplexer_1_out_1, demultiplexer_1_out_2, demultiplexer_1_out_3, demultiplexer_1_out_4,
       demultiplexer_1_out_6, demultiplexer_1_out_8, demultiplexer_1_out_9, demultiplexer_1_out_10,
       demultiplexer_1_out_11, demultiplexer_1_out_12, demultiplexer_1_out_13, demultiplexer_1_out_14,
       demultiplexer_1_out_15;
  wire [15:0] demultiplexer_2_out_1, demultiplexer_2_out_2, demultiplexer_2_out_3, demultiplexer_2_out_4,
       demultiplexer_2_out_6, demultiplexer_2_out_8, demultiplexer_2_out_9, demultiplexer_2_out_10,
       demultiplexer_2_out_11, demultiplexer_2_out_12, demultiplexer_2_out_13, demultiplexer_2_out_14,
       demultiplexer_2_out_15, R1_q, R2_q, R3_q, R4_q, R6_q, R8_q, R9_q, R10_q, R11_q, R12_q, R13_q, R14_q,
       R15_q;

  Demultiplexer #(.Selector_Bits(4)) demultiplexer_1 (
    .sel(WS), .in(WE), .out_1(demultiplexer_1_out_1), .out_2(demultiplexer_1_out_2),
    .out_3(demultiplexer_1_out_3), .out_4(demultiplexer_1_out_4), .out_6(demultiplexer_1_out_6),
    .out_8(demultiplexer_1_out_8), .out_9(demultiplexer_1_out_9), .out_10(demultiplexer_1_out_10),
    .out_11(demultiplexer_1_out_11), .out_12(demultiplexer_1_out_12), .out_13(demultiplexer_1_out_13),
    .out_14(demultiplexer_1_out_14), .out_15(demultiplexer_1_out_15));  // open: out_0, out_5, out_7
  Demultiplexer #(.Selector_Bits(4), .Bits(16)) demultiplexer_2 (
    .sel(WS), .in(IN), .out_1(demultiplexer_2_out_1), .out_2(demultiplexer_2_out_2),
    .out_3(demultiplexer_2_out_3), .out_4(demultiplexer_2_out_4), .out_6(demultiplexer_2_out_6),
    .out_8(demultiplexer_2_out_8), .out_9(demultiplexer_2_out_9), .out_10(demultiplexer_2_out_10),
    .out_11(demultiplexer_2_out_11), .out_12(demultiplexer_2_out_12), .out_13(demultiplexer_2_out_13),
    .out_14(demultiplexer_2_out_14), .out_15(demultiplexer_2_out_15));  // open: out_0, out_5, out_7
  Register #(.Bits(16)) R1 (.D(demultiplexer_2_out_1), .C(clk), .en(demultiplexer_1_out_1), .Q(R1_q));
  Register #(.Bits(16)) R2 (.D(demultiplexer_2_out_2), .C(clk), .en(demultiplexer_1_out_2), .Q(R2_q));
  Register #(.Bits(16)) R3 (.D(demultiplexer_2_out_3), .C(clk), .en(demultiplexer_1_out_3), .Q(R3_q));
  Register #(.Bits(16)) R4 (.D(demultiplexer_2_out_4), .C(clk), .en(demultiplexer_1_out_4), .Q(R4_q));
  Register #(.Bits(16)) FL (.D(FLIN), .C(clk), .en(FLEN), .Q(FLOUT));
  Register #(.Bits(16)) R6 (.D(demultiplexer_2_out_6), .C(clk), .en(demultiplexer_1_out_6), .Q(R6_q));
  Register #(.Bits(16)) R8 (.D(demultiplexer_2_out_8), .C(clk), .en(demultiplexer_1_out_8), .Q(R8_q));
  Register #(.Bits(16)) R9 (.D(demultiplexer_2_out_9), .C(clk), .en(demultiplexer_1_out_9), .Q(R9_q));
  Register #(.Bits(16)) R10 (.D(demultiplexer_2_out_10), .C(clk), .en(demultiplexer_1_out_10), .Q(R10_q));
  Register #(.Bits(16)) R11 (.D(demultiplexer_2_out_11), .C(clk), .en(demultiplexer_1_out_11), .Q(R11_q));
  Register #(.Bits(16)) R12 (.D(demultiplexer_2_out_12), .C(clk), .en(demultiplexer_1_out_12), .Q(R12_q));
  Register #(.Bits(16)) R13 (.D(demultiplexer_2_out_13), .C(clk), .en(demultiplexer_1_out_13), .Q(R13_q));
  Register #(.Bits(16)) R14 (.D(demultiplexer_2_out_14), .C(clk), .en(demultiplexer_1_out_14), .Q(R14_q));
  Register #(.Bits(16)) R15 (.D(demultiplexer_2_out_15), .C(clk), .en(demultiplexer_1_out_15), .Q(R15_q));
  Multiplexer #(.Selector_Bits(4), .Bits(16)) multiplexer_1 (
    .sel(RS1), .in_0({16{1'b0}}), .in_1(R1_q), .in_2(R2_q), .in_3(R3_q), .in_4(R4_q), .in_5(FLOUT),
    .in_6(R6_q), .in_7(R7), .in_8(R8_q), .in_9(R9_q), .in_10(R10_q), .in_11(R11_q), .in_12(R12_q),
    .in_13(R13_q), .in_14(R14_q), .in_15(R15_q), .out(OUT1));
  Multiplexer #(.Selector_Bits(4), .Bits(16)) multiplexer_2 (
    .sel(RS2), .in_0({16{1'b0}}), .in_1(R1_q), .in_2(R2_q), .in_3(R3_q), .in_4(R4_q), .in_5(FLOUT),
    .in_6(R6_q), .in_7(R7), .in_8(R8_q), .in_9(R9_q), .in_10(R10_q), .in_11(R11_q), .in_12(R12_q),
    .in_13(R13_q), .in_14(R14_q), .in_15(R15_q), .out(OUT2));

  // Notes on the sheet:
  //   RS1: The index of the register which should output its value to OUT1.
  //   RS2: The index of the register which should output its value to OUT2.
  //   WS: The index of the register which should save the value on IN on the next clock cycle (if WE is high).
  //   WE: Whether the register selected by WS should save the value from IN on the next cycle.
  //   IN: The value to be saved into the register specified by WS if WE is high,
  //   OUT1: The value in the register specified by RS1.
  //   OUT2: The value in the register specified by RS2.
endmodule

/* Test case:
clk RS1 RS2 WS WE IN OUT1 OUT2
c 0 0 0 1 0x1234 0x0000 0x0000
c 1 0 1 1 0xBEEF 0xBEEF 0x0000
c 2 1 2 1 0xDEAD 0xDEAD 0xBEEF
c 3 2 3 1 0xFFFF 0xFFFF 0xDEAD
c 3 2 3 0 0xABCD 0xFFFF 0xDEAD
c 3 2 2 0 0xABCD 0xFFFF 0xDEAD
c 1 0 1 0 0xABCD 0xBEEF 0x0000
c 1 0 0 0 0xABCD 0xBEEF 0x0000
c 1 0 2 1 0xBADE 0xBEEF 0x0000
c 0 2 2 1 0xBADE 0x0000 0xBADE
c 0 0 2 0 0x1234 0x0000 0x0000
c 2 3 0 1 0x0000 0xBADE 0xFFFF
c 0 0 2 0 0x1234 0x0000 0x0000
*/
